# Fritzing sketch dice (saved by Fritzing 0.9.4)
circuit board: 8.46667cm x 5.64444cm
perfboards: 1

parts:
  Part1 = Arduino Nano (Rev3.0)
  S1 = Toggle Switch [package=THT]
  R1 = Resistor [tolerance=±5% resistance=220 package="1206 [SMD]"]
  R3 = Resistor [tolerance=±5% resistance=220 package="1206 [SMD]"]
  R4 = Resistor [tolerance=±5% resistance=220 package="1206 [SMD]"]
  R5 = Resistor [tolerance=±5% resistance=220 package="1206 [SMD]"]
  R6 = Resistor [tolerance=±5% resistance=220 package="1206 [SMD]"]
  R7 = Resistor [tolerance=±5% resistance=220 package="1206 [SMD]"]
  R8 = Resistor [tolerance=±5% resistance=220 package="1206 [SMD]"]
  Disp1 = KWM-R30881CUAB [part_number=KWM-R30881CUAB]
  U2 = LIPO-1000mAh [package=lipo-1000]
  Part2 = USB LiPoly Charger
  R9 = Resistor [tolerance=±5% resistance=220 package="1206 [SMD]"]

nets:
  GND: Part1.GND, U2.-, Part2.GND
  N1: Part1.D2, R9.Pin_0
  N2: Part1.D3, R1.Pin_0
  N3: Part1.D5, Disp1.pin_5
  N4: Part1.D6, Disp1.pin2
  N5: Part1.D7, Disp1.pin_7
  N6: Part1.D8, Disp1.pin1
  N7: Part1.D9, Disp1.pin_12
  N8: Part1.D10, Disp1.pin_8
  N9: Part1.D11/MOSI, Disp1.pin_14
  N10: Part1.D12/MISO, Disp1.pin_9
  N11: Part1.VIN, S1.COM
  N12: Part1.A5, R3.Pin_0
  N13: Part1.A4, R4.Pin_0
  N14: Part1.A3, R5.Pin_0
  N15: Part1.A2, R6.Pin_0
  N16: Part1.A1, R7.Pin_0
  N17: Part1.A0, R8.Pin_0
  N18: S1.L1, U2.+, Part2.VBAT
  N19: R1.Pin_1, Disp1.pin_16
  N20: R3.Pin_1, Disp1.pin_11
  N21: R4.Pin_1, Disp1.pin_6
  N22: R5.Pin_1, Disp1.pin_10
  N23: R6.Pin_1, Disp1.pin_4
  N24: R7.Pin_1, Disp1.pin_3
  N25: R8.Pin_1, Disp1.pin_13
  N26: Disp1.pin_15, R9.Pin_1

custom parts:
  KWM-R30881CUAB: LED Matrix Display 8x8 red 60.5mm modified for KWM-R30881CUAB row cathode feb 2018.

// code stored in the sketch: dice.ino
#include <TrueRandom.h>

#define ROW_1 12
#define ROW_2 11
#define ROW_3 10
#define ROW_4 9
#define ROW_5 8
#define ROW_6 7
#define ROW_7 6
#define ROW_8 5
#define COL_1 A0
#define COL_2 A1
#define COL_3 A2
#define COL_4 A3
#define COL_5 A4
#define COL_6 A5
#define COL_7 2
#define COL_8 3

const byte rows[] = {
    ROW_1, ROW_2, ROW_3, ROW_4, ROW_5, ROW_6, ROW_7, ROW_8
};

byte d_1_1[] =   {B00000000,
                  B01000000,
                  B00000000,
                  B00000000,
                  B00000000,
                  B00000000,
                  B00000010,
                  B00000000};

byte d_1_2[] =   {B00000000,
                  B01000000,
                  B00000000,
                  B00000000,
                  B00000000,
                  B00000100,
                  B00000000,
                  B00000001};

byte d_1_3[] =   {B00000000,
                  B01000000,
                  B00000000,
                  B00000000,
                  B00000000,
                  B00000100,
                  B00000010,
                  B00000001};

byte d_1_4[] =   {B00000000,
                  B01000000,
                  B00000000,
                  B00000000,
                  B00000000,
                  B00000101,
                  B00000000,
                  B00000101};

byte d_1_5[] =   {B00000000,
                  B01000000,
                  B00000000,
                  B00000000,
                  B00000000,
                  B00000101,
                  B00000010,
                  B00000101};

byte d_1_6[] =   {B00000000,
                  B01000000,
                  B00000000,
                  B00000000,
                  B00000000,
                  B00000101,
                  B00000101,
                  B00000101};              

byte d_2_1[] =   {B10000000,
                  B00000000,
                  B00100000,
                  B00000000,
                  B00000000,
                  B00000000,
                  B00000010,
                  B00000000};

byte d_2_2[] =   {B10000000,
                  B00000000,
                  B00100000,
                  B00000000,
                  B00000000,
                  B00000100,
                  B00000000,
                  B00000001};
              
byte d_2_3[] =   {B10000000,
                  B00000000,
                  B00100000,
                  B00000000,
                  B00000000,
                  B00000100,
                  B00000010,
                  B00000001};

byte d_2_4[] =   {B10000000,
                  B00000000,
                  B00100000,
                  B00000000,
                  B00000000,
                  B00000101,
                  B00000000,
                  B00000101};

byte d_2_5[] =   {B10000000,
                  B00000000,
                  B00100000,
                  B00000000,
                  B00000000,
                  B00000101,
                  B00000010,
                  B00000101};

byte d_2_6[] =   {B10000000,
                  B00000000,
                  B00100000,
                  B00000000,
                  B00000000,
                  B00000101,
                  B00000101,
                  B00000101};
                  
byte d_3_1[] =   {B10000000,
                  B01000000,
                  B00100000,
                  B00000000,
                  B00000000,
                  B00000000,
                  B00000010,
                  B00000000};

byte d_3_2[] =   {B10000000,
                  B01000000,
                  B00100000,
                  B00000000,
                  B00000000,
                  B00000100,
                  B00000000,
                  B00000001};

byte d_3_3[] =   {B10000000,
                  B01000000,
                  B00100000,
                  B00000000,
                  B00000000,
                  B00000100,
                  B00000010,
                  B00000001};

byte d_3_4[] =   {B10000000,
                  B01000000,
                  B00100000,
                  B00000000,
                  B00000000,
                  B00000101,
                  B00000000,
                  B00000101};

byte d_3_5[] =   {B10000000,
                  B01000000,
                  B00100000,
                  B00000000,
                  B00000000,
                  B00000101,
                  B00000010,
                  B00000101};                  

byte d_3_6[] =   {B10000000,
                  B01000000,
                  B00100000,
                  B00000000,
                  B00000000,
                  B00000101,
                  B00000101,
                  B00000101};

byte d_4_1[] =   {B10100000,
                  B00000000,
                  B10100000,
                  B00000000,
                  B00000000,
                  B00000000,
                  B00000010,
                  B00000000};

byte d_4_2[] =   {B10100000,
                  B00000000,
                  B10100000,
                  B00000000,
                  B00000000,
                  B00000100,
                  B00000000,
                  B00000001};

byte d_4_3[] =   {B10100000,
                  B00000000,
                  B10100000,
                  B00000000,
                  B00000000,
                  B00000100,
                  B00000010,
                  B00000001};

byte d_4_4[] =   {B10100000,
                  B00000000,
                  B10100000,
                  B00000000,
                  B00000000,
                  B00000101,
                  B00000000,
                  B00000101};

byte d_4_5[] =   {B10100000,
                  B00000000,
                  B10100000,
                  B00000000,
                  B00000000,
                  B00000101,
                  B00000010,
                  B00000101};

byte d_4_6[] =   {B10100000,
                  B00000000,
                  B10100000,
                  B00000000,
                  B00000000,
                  B00000101,
                  B00000101,
                  B00000101};

byte d_5_1[] =   {B10100000,
                  B01000000,
                  B10100000,
                  B00000000,
                  B00000000,
                  B00000000,
                  B00000010,
                  B00000000};

byte d_5_2[] =   {B10100000,
                  B01000000,
                  B10100000,
                  B00000000,
                  B00000000,
                  B00000100,
                  B00000010,
                  B00000001};

byte d_5_3[] =   {B10100000,
                  B01000000,
                  B10100000,
                  B00000000,
                  B00000000,
                  B00000100,
                  B00000010,
                  B00000001};

byte d_5_4[] =   {B10100000,
                  B01000000,
                  B10100000,
                  B00000000,
                  B00000000,
                  B00000101,
                  B00000000,
                  B00000101};

byte d_5_5[] =   {B10100000,
                  B01000000,
                  B10100000,
                  B00000000,
                  B00000000,
                  B00000101,
                  B00000010,
                  B00000101};

byte d_5_6[] =   {B10100000,
                  B01000000,
                  B10100000,
                  B00000000,
                  B00000000,
                  B00000101,
                  B00000101,
                  B00000101};

byte d_6_1[] =   {B10100000,
                  B10100000,
                  B10100000,
                  B00000000,
                  B00000000,
                  B00000000,
                  B00000010,
                  B00000000};

byte d_6_2[] =   {B10100000,
                  B10100000,
                  B10100000,
                  B00000000,
                  B00000000,
                  B00000100,
                  B00000000,
                  B00000001};

byte d_6_3[] =   {B10100000,
                  B10100000,
                  B10100000,
                  B00000000,
                  B00000000,
                  B00000100,
                  B00000010,
                  B00000001};

byte d_6_4[] =   {B10100000,
                  B10100000,
                  B10100000,
                  B00000000,
                  B00000000,
                  B00000101,
                  B00000000,
                  B00000101};

byte d_6_5[] =   {B10100000,
                  B10100000,
                  B10100000,
                  B00000000,
                  B00000000,
                  B00000101,
                  B00000010,
                  B00000101};

byte d_6_6[] =   {B10100000,
                  B10100000,
                  B10100000,
                  B00000000,
                  B00000000,
                  B00000101,
                  B00000101,
                  B00000101};

void setup() {

    pinMode(A0, OUTPUT);
    pinMode(A1, OUTPUT);
    pinMode(A2, OUTPUT);
    pinMode(A3, OUTPUT);
    pinMode(A4, OUTPUT);
    pinMode(A5, OUTPUT);
    pinMode(A6, INPUT_PULLUP);
    pinMode(A7, INPUT_PULLUP);

    pinMode(2, OUTPUT);
    pinMode(3, OUTPUT);
    pinMode(4, INPUT_PULLUP);
    pinMode(5, OUTPUT);
    pinMode(6, OUTPUT);
    pinMode(7, OUTPUT);
    pinMode(8, OUTPUT);
    pinMode(9, OUTPUT);
    pinMode(10, OUTPUT);
    pinMode(11, OUTPUT);
    pinMode(12, OUTPUT);
    pinMode(13, INPUT_PULLUP);
    
    Serial.begin(9600);
}

int randdomN = TrueRandom.random(1,37);

      
void loop() 
{
  Serial.print(randdomN);
  
  if (randdomN == 1) {
    drawScreen(d_1_1);
  }
    else if (randdomN == 2) {
    drawScreen(d_1_2);
  }
    else if (randdomN == 3) {
    drawScreen(d_1_3);
  }
    else if (randdomN == 4) {
    drawScreen(d_1_4);
  }
    else if (randdomN == 5) {
    drawScreen(d_1_5);
  }
    else if (randdomN == 6) {
    drawScreen(d_1_6);
  }
    else if (randdomN == 7) {
    drawScreen(d_2_1);
  }
    else if (randdomN == 8) {
    drawScreen(d_2_2);
  }
    else if (randdomN == 9) {
    drawScreen(d_2_3);
  }
    else if (randdomN == 10) {
    drawScreen(d_2_4);
  }
    else if (randdomN == 11) {
    drawScreen(d_2_5);
  }
    else if (randdomN == 12) {
    drawScreen(d_2_6);
  }
    else if (randdomN == 13) {
    drawScreen(d_3_1);
  }
    else if (randdomN == 14) {
    drawScreen(d_3_2);
  }
    else if (randdomN == 15) {
    drawScreen(d_3_3);
  }
    else if (randdomN == 16) {
    drawScreen(d_3_4);
  }
    else if (randdomN == 17) {
    drawScreen(d_3_5);
  }
    else if (randdomN == 18) {
    drawScreen(d_3_6);
  }
    else if (randdomN == 19) {
    drawScreen(d_4_1);
  }
    else if (randdomN == 20) {
    drawScreen(d_4_2);
  }
    else if (randdomN == 21) {
    drawScreen(d_4_3);
  }
    else if (randdomN == 22) {
    drawScreen(d_4_4);
  }
    else if (randdomN == 23) {
    drawScreen(d_4_5);
  }
    else if (randdomN == 24) {
    drawScreen(d_4_6);
  }
    else if (randdomN == 25) {
    drawScreen(d_5_1);
  }
    else if (randdomN == 26) {
    drawScreen(d_5_2);
  }
    else if (randdomN == 27) {
    drawScreen(d_5_3);
  }
    else if (randdomN == 28) {
    drawScreen(d_5_4);
  }
    else if (randdomN == 29) {
    drawScreen(d_5_5);
  }
    else if (randdomN == 30) {
    drawScreen(d_5_6);
  }
    else if (randdomN == 31) {
    drawScreen(d_6_1);
  }
    else if (randdomN == 32) {
    drawScreen(d_6_2);
  }
    else if (randdomN == 33) {
    drawScreen(d_6_3);
  }
    else if (randdomN == 34) {
    drawScreen(d_6_4);
  }
    else if (randdomN == 35) {
    drawScreen(d_6_5);
  }
    else {
    drawScreen(d_6_6);
  }
}

 void  drawScreen(byte buffer2[]){
     
    
   // Turn on each row in series
    for (byte i = 0; i < 8; i++) {
        setColumns(buffer2[i]); // Set columns for this specific row
        
        digitalWrite(rows[i], LOW);
        delay(1); // Set this to 50 or 100 if you want to see the multiplexing effect!
        digitalWrite(rows[i], HIGH);
        
    }
}

void setColumns(byte b) {
    digitalWrite(COL_1, (b >> 0) & 0x01); // Get the 1st bit: 10000000
    digitalWrite(COL_2, (b >> 1) & 0x01); // Get the 2nd bit: 01000000
    digitalWrite(COL_3, (b >> 2) & 0x01); // Get the 3rd bit: 00100000
    digitalWrite(COL_4, (b >> 3) & 0x01); // Get the 4th bit: 00010000
    digitalWrite(COL_5, (b >> 4) & 0x01); // Get the 5th bit: 00001000
    digitalWrite(COL_6, (b >> 5) & 0x01); // Get the 6th bit: 00000100
    digitalWrite(COL_7, (b >> 6) & 0x01); // Get the 7th bit: 00000010
    digitalWrite(COL_8, (b >> 7) & 0x01); // Get the 8th bit: 00000001
    
    // If the polarity of your matrix is the opposite of mine
    // remove all the '~' above.
}
